# Fritzing sketch analog_led (saved by Fritzing 0.9.3b)
breadboards: 1

parts:
  LED1 = smd LED [color="Red (633nm)" package="0805 [SMD]"]
  R1 = Resistor [tolerance=±5% resistance=220 package="1206 [SMD]"]
  Part1 = Arduino Uno (Rev3)
  R2 = Rotary Potentiometer (Small) [maximum_resistance=10kΩ package=THT]
  S1 = SWITCH_SPDT [package=kps-1290]
  J1 = Piezo Speaker

nets:
  N1: LED1.cathode, Part1.GND, R2.leg1, J1.pin1
  N2: LED1.anode, R1.Pin_0
  N3: R1.Pin_1, Part1.D9_PWM
  N4: Part1.A0, R2.wiper
  N5: Part1.D11_PWM/MOSI, S1.S
  N6: Part1.5V, R2.leg2
  N7: S1.P, J1.pin2
