# Fritzing sketch led_sos (saved by Fritzing 0.9.3b)
breadboards: 1

parts:
  LED_SOS = Arduino Uno (Rev3) - ICSP
  LED2 = LED - 3mm [color="Red (633nm)" package="3 mm [THT]"]
  R1 = Resistor [tolerance=±5% resistance=220 package="0402 [SMD]"]

nets:
  N1: LED_SOS.GND, LED2.cathode
  N2: LED_SOS.D13/SCK, R1.Pin_1
  N3: LED2.anode, R1.Pin_0
