# Fritzing sketch theramin (saved by Fritzing 0.9.3b)
breadboards: 1

parts:
  Part1 = Arduino Uno (Rev3)
  R1 = PHOTOCELL [package=photocell]
  J1 = Piezo Speaker
  R2 = Resistor [tolerance=±5% resistance=10k package=THT]

nets:
  N1: Part1.A0, J1.pin2
  N2: Part1.D9_PWM, R1.P$2, R2.Pin_0
  N3: Part1.5V, R1.P$1
  N4: Part1.GND, J1.pin1, R2.Pin_1
