# Fritzing sketch button (saved by Fritzing 0.9.3b)
breadboards: 1

parts:
  R1 = Resistor [tolerance=±5% resistance=220 package="2512 [SMD]"]
  R2 = Resistor [tolerance=±5% resistance=10k package=THT]
  S2 = Pushbutton [package="[SMD]"]
  LED1 = LED - 5mm [color="Red (633nm)" package="5 mm [THT]"]
  Part1 = Arduino Uno (Rev3)
  J1 = Piezo Speaker
  S3 = Pushbutton [package="[SMD]"]
  S4 = Pushbutton [package="[SMD]"]
  R3 = Resistor [tolerance=±5% resistance=10k package=THT]
  R4 = Resistor [tolerance=±5% resistance=10k package=THT]

nets:
  N1: R1.Pin_0, LED1.anode
  N2: R2.Pin_0, LED1.cathode, Part1.GND, J1.pin1, R3.Pin_0, R4.Pin_0
  N3: R2.Pin_1, S2.Pin_1, S2.Pin_2, Part1.D3_PWM
  N4: S2.Pin_3, S2.Pin_4, Part1.5V, S3.Pin_3, S3.Pin_4, S4.Pin_3, S4.Pin_4
  N5: Part1.D11_PWM/MOSI, J1.pin2
  N6: Part1.D5_PWM, S3.Pin_1, S3.Pin_2, R3.Pin_1
  N7: Part1.D7, S4.Pin_1, S4.Pin_2, R4.Pin_1
